// Logisim project Question3.circ as structural Verilog: 1 circuit, main circuit main
module main (
  input  A,
  input  B,
  input  A_2,
  input  C,
  input  B_2,
  input  D,
  input  C_2,
  input  D_2,
  input  A_3,
  input  B_3,
  input  C_3,
  input  D_3
);

  wire A_prime_2_out, A_prime_out, and_1_out, and_2_out, and_3_out, and_4_out, and_5_out, and_6_out,
       and_7_out, multiplexer_1_out, multiplexer_2_out, multiplexer_3_out, multiplexer_4_out, not_1_out,
       not_2_out, not_3_out, not_4_out, not_5_out, or_1_out, xnor_1_out;

  not not_1 (not_1_out, 1'b1);
  not A_prime (A_prime_out, A);
  Multiplexer #(.select(3), .disabled(0), .enable("false")) multiplexer_1 (
    .in0(1'b1), .in1(not_1_out), .in2(not_1_out), .in3(A), .in4(A_prime_out), .in5(A), .in6(A_prime_out),
    .in7(A_prime_out), .out(multiplexer_1_out), .sel({D_2, C_2, B_2}));
  LED led_1 (.in(multiplexer_1_out));
  not not_2 (not_2_out, 1'b1);
  not A_prime_2 (A_prime_2_out, A_2);
  not not_3 (not_3_out, A_3);
  not not_4 (not_4_out, B_3);
  Multiplexer #(.select(2), .enable("false")) multiplexer_2 (
    .in0(1'b1), .in1(not_2_out), .in2(not_2_out), .in3(A_2), .out(multiplexer_2_out), .sel({C, B}));
  not not_5 (not_5_out, D);
  Multiplexer #(.select(2), .enable("false")) multiplexer_3 (
    .in0(A_prime_2_out), .in1(A_2), .in2(A_prime_2_out), .in3(A_prime_2_out), .out(multiplexer_3_out),
    .sel({C, B}));
  and and_1 (and_1_out, 1'b1, not_3_out);
  and and_2 (and_2_out, 1'b1, not_4_out);
  and and_3 (and_3_out, multiplexer_2_out, not_5_out);
  or or_1 (or_1_out, and_3_out, and_4_out);
  and and_4 (and_4_out, D, multiplexer_3_out);
  and and_5 (and_5_out, 1'b1, ~B_3);  // AND_Gate
  and and_6 (and_6_out, 1'b1, A_3, B_3);
  xnor xnor_1 (xnor_1_out, and_1_out, and_2_out);
  and and_7 (and_7_out, 1'b1, not_3_out);
  LED led_2 (.in(or_1_out));
  Multiplexer #(.select(2), .enable("false")) multiplexer_4 (
    .in0(and_5_out), .in1(and_6_out), .in2(xnor_1_out), .in3(and_7_out), .out(multiplexer_4_out),
    .sel({D_3, C_3}));
  LED led_3 (.in(multiplexer_4_out));
endmodule
